// Logisim project 9-1.circ as structural Verilog: 1 circuit, main circuit main
module main (
  output out_1,
  output out_2,
  output out_3,
  output out_4
);

  wire and_1_out, clock_1_out, t_ff_1_qn, t_ff_2_qn, t_ff_3_qn, t_ff_4_qn;

  Clock clock_1 (.out(clock_1_out));
  T_Flip_Flop t_ff_1 (
    .clk(clock_1_out), .T(clock_1_out), .Q(out_1), .Qn(t_ff_1_qn), .preset(and_1_out));  // open: reset, en
  T_Flip_Flop t_ff_2 (.clk(out_1), .T(out_1), .Q(out_2), .Qn(t_ff_2_qn), .reset(and_1_out));  // open: preset, en
  T_Flip_Flop t_ff_3 (.clk(out_2), .T(out_2), .Q(out_3), .Qn(t_ff_3_qn), .en(and_1_out));  // open: preset, reset
  T_Flip_Flop t_ff_4 (.clk(out_3), .T(out_3), .Q(out_4), .Qn(t_ff_4_qn), .en(and_1_out));  // open: preset, reset
  and and_1 (and_1_out, t_ff_3_qn, t_ff_4_qn, t_ff_2_qn, t_ff_1_qn);
  Hex_Digit_Display hex_digit_display_1 (.value({out_4, out_3, out_2, out_1}));  // open: dp
endmodule
