// Logisim project Full Adder.circ as structural Verilog: 1 circuit, main circuit main
module main (
  input  A,
  input  B,
  input  C,
  output SUM,
  output Carry
);

  wire and_1_out, and_2_out, xor_1_out;

  buf xor_1 (xor_1_out, A);  // XOR_Gate
  buf and_1 (and_1_out, A);  // AND_Gate
  and and_2 (and_2_out, xor_1_out, C);
  xor xor_2 (SUM, xor_1_out, C);
  or or_1 (Carry, and_2_out, and_1_out);
endmodule
