// Logisim project Prime Number.circ as structural Verilog: 1 circuit, main circuit main
module main (
  input  N0,
  input  N1,
  input  N2,
  input  N3,
  output F
);

  wire and_1_out, and_2_out, and_3_out, xor_1_out;

  and and_1 (and_1_out, N0, ~N3);  // AND_Gate
  and and_2 (and_2_out, N1, ~N2, ~N3);  // AND_Gate
  xor xor_1 (xor_1_out, N1, N2);
  and and_3 (and_3_out, N0, xor_1_out);
  or or_1 (F, and_1_out, and_3_out, and_2_out);

  // Notes on the sheet:
  //   Prime Number Detector
endmodule
